// Logisim project cpu.circ as structural Verilog: 20 circuits, main circuit main3
module SingleReg (
  input  clk,
  input  WE,
  input  Reset,
  input  [15:0] RegIn,
  output [15:0] RegOut
);

  wire and_1_out, and_2_out, and_3_out, and_4_out, and_5_out, and_6_out, and_7_out, and_8_out, and_9_out,
       and_10_out, and_11_out, and_12_out, and_13_out, and_14_out, and_15_out, and_16_out;

  and and_1 (and_1_out, WE, clk);
  and and_2 (and_2_out, WE, clk);
  and and_3 (and_3_out, WE, clk);
  and and_4 (and_4_out, WE, clk);
  D_Flip_Flop d_ff_1 (.D(RegIn[0]), .clk(and_1_out), .Q(RegOut[0]), .reset(Reset));  // open: Qn, preset
  D_Flip_Flop d_ff_2 (.D(RegIn[4]), .clk(and_2_out), .Q(RegOut[4]), .reset(Reset));  // open: Qn, preset
  D_Flip_Flop d_ff_3 (.D(RegIn[8]), .clk(and_3_out), .Q(RegOut[8]), .reset(Reset));  // open: Qn, preset
  D_Flip_Flop d_ff_4 (.D(RegIn[12]), .clk(and_4_out), .Q(RegOut[12]), .reset(Reset));  // open: Qn, preset
  and and_5 (and_5_out, WE, clk);
  and and_6 (and_6_out, WE, clk);
  and and_7 (and_7_out, WE, clk);
  and and_8 (and_8_out, WE, clk);
  D_Flip_Flop d_ff_5 (.D(RegIn[1]), .clk(and_5_out), .Q(RegOut[1]), .reset(Reset));  // open: Qn, preset
  D_Flip_Flop d_ff_6 (.D(RegIn[5]), .clk(and_6_out), .Q(RegOut[5]), .reset(Reset));  // open: Qn, preset
  D_Flip_Flop d_ff_7 (.D(RegIn[9]), .clk(and_7_out), .Q(RegOut[9]), .reset(Reset));  // open: Qn, preset
  D_Flip_Flop d_ff_8 (.D(RegIn[13]), .clk(and_8_out), .Q(RegOut[13]), .reset(Reset));  // open: Qn, preset
  and and_9 (and_9_out, WE, clk);
  and and_10 (and_10_out, WE, clk);
  and and_11 (and_11_out, WE, clk);
  and and_12 (and_12_out, WE, clk);
  D_Flip_Flop d_ff_9 (.D(RegIn[2]), .clk(and_9_out), .Q(RegOut[2]), .reset(Reset));  // open: Qn, preset
  D_Flip_Flop d_ff_10 (.D(RegIn[6]), .clk(and_10_out), .Q(RegOut[6]), .reset(Reset));  // open: Qn, preset
  D_Flip_Flop d_ff_11 (.D(RegIn[10]), .clk(and_11_out), .Q(RegOut[10]), .reset(Reset));  // open: Qn, preset
  D_Flip_Flop d_ff_12 (.D(RegIn[14]), .clk(and_12_out), .Q(RegOut[14]), .reset(Reset));  // open: Qn, preset
  and and_13 (and_13_out, WE, clk);
  and and_14 (and_14_out, WE, clk);
  and and_15 (and_15_out, WE, clk);
  and and_16 (and_16_out, WE, clk);
  D_Flip_Flop d_ff_13 (.D(RegIn[3]), .clk(and_13_out), .Q(RegOut[3]), .reset(Reset));  // open: Qn, preset
  D_Flip_Flop d_ff_14 (.D(RegIn[7]), .clk(and_14_out), .Q(RegOut[7]), .reset(Reset));  // open: Qn, preset
  D_Flip_Flop d_ff_15 (.D(RegIn[11]), .clk(and_15_out), .Q(RegOut[11]), .reset(Reset));  // open: Qn, preset
  D_Flip_Flop d_ff_16 (.D(RegIn[15]), .clk(and_16_out), .Q(RegOut[15]), .reset(Reset));  // open: Qn, preset

  // Other names for the same wires on the sheet: in0 = RegIn[0]; in1 = RegIn[1]; in2 = RegIn[2]; in3 = RegIn[3];
  //   in4 = RegIn[4]; in5 = RegIn[5]; in6 = RegIn[6]; in7 = RegIn[7]; in8 = RegIn[8]; in9 = RegIn[9];
  //   in10 = RegIn[10]; in11 = RegIn[11]; in12 = RegIn[12]; in13 = RegIn[13]; in14 = RegIn[14]; in15 = RegIn[15];
  //   out0 = RegOut[0]; out1 = RegOut[1]; out2 = RegOut[2]; out3 = RegOut[3]; out4 = RegOut[4]; out5 = RegOut[5];
  //   out6 = RegOut[6]; out7 = RegOut[7]; out8 = RegOut[8]; out9 = RegOut[9]; out10 = RegOut[10]; out11 = RegOut[11];
  //   out12 = RegOut[12]; out13 = RegOut[13]; out14 = RegOut[14]; out15 = RegOut[15]
endmodule

module RegisterFile (
  input  clk,
  input  Reset,
  input  [15:0] WriteData,
  input  [2:0] WriteReg,
  input  [2:0] ReadReg1,
  input  [2:0] ReadReg2,
  input  RegWriteEnable,
  output [15:0] ReadData1,
  output [15:0] ReadData2
);

  wire en0, en1, en2, en3, en4, en5, en6, en7, ren10, ren11, ren12, ren13, ren14, ren15, ren16, ren17, ren20,
       ren21, ren22, ren23, ren24, ren25, ren26, ren27, WEn0, WEn1, WEn2, WEn3, WEn4, WEn5, WEn6, WEn7;
  wire [15:0] out1, out2, out3, out4, out5, out6, out7;

  Decoder #(.select(3)) decoder_1 (
    .out0(ren10), .out1(ren11), .out2(ren12), .out3(ren13), .out4(ren14), .out5(ren15), .out6(ren16),
    .out7(ren17), .sel(ReadReg1));  // open: en
  Decoder #(.select(3)) decoder_2 (
    .out0(ren20), .out1(ren21), .out2(ren22), .out3(ren23), .out4(ren24), .out5(ren25), .out6(ren26),
    .out7(ren27), .sel(ReadReg2));  // open: en
  // Probe on out5
  // Probe on out1
  SingleReg singlereg_1 (.clk(clk), .WE(WEn1), .Reset(Reset), .RegIn(WriteData), .RegOut(out1));
  SingleReg singlereg_2 (.clk(clk), .WE(WEn5), .Reset(Reset), .RegIn(WriteData), .RegOut(out5));
  assign ReadData1 = ren10 ? {16{1'b0}} : 16'bz;  // Controlled_Buffer controlled_buffer_1
  assign ReadData1 = ren11 ? out1 : 16'bz;  // Controlled_Buffer controlled_buffer_2
  assign ReadData1 = ren12 ? out2 : 16'bz;  // Controlled_Buffer controlled_buffer_3
  assign ReadData1 = ren13 ? out3 : 16'bz;  // Controlled_Buffer controlled_buffer_4
  assign ReadData1 = ren14 ? out4 : 16'bz;  // Controlled_Buffer controlled_buffer_5
  assign ReadData1 = ren15 ? out5 : 16'bz;  // Controlled_Buffer controlled_buffer_6
  assign ReadData1 = ren16 ? out6 : 16'bz;  // Controlled_Buffer controlled_buffer_7
  assign ReadData1 = ren17 ? out7 : 16'bz;  // Controlled_Buffer controlled_buffer_8
  // Probe on out2
  SingleReg singlereg_3 (.clk(clk), .WE(WEn2), .Reset(Reset), .RegIn(WriteData), .RegOut(out2));
  // Probe on out6
  SingleReg singlereg_4 (.clk(clk), .WE(WEn6), .Reset(Reset), .RegIn(WriteData), .RegOut(out6));
  Decoder #(.select(3)) decoder_3 (
    .out0(en0), .out1(en1), .out2(en2), .out3(en3), .out4(en4), .out5(en5), .out6(en6), .out7(en7),
    .sel(WriteReg));  // open: en
  assign ReadData2 = ren20 ? {16{1'b0}} : 16'bz;  // Controlled_Buffer controlled_buffer_9
  assign ReadData2 = ren21 ? out1 : 16'bz;  // Controlled_Buffer controlled_buffer_10
  assign ReadData2 = ren22 ? out2 : 16'bz;  // Controlled_Buffer controlled_buffer_11
  assign ReadData2 = ren23 ? out3 : 16'bz;  // Controlled_Buffer controlled_buffer_12
  assign ReadData2 = ren24 ? out4 : 16'bz;  // Controlled_Buffer controlled_buffer_13
  assign ReadData2 = ren25 ? out5 : 16'bz;  // Controlled_Buffer controlled_buffer_14
  assign ReadData2 = ren26 ? out6 : 16'bz;  // Controlled_Buffer controlled_buffer_15
  assign ReadData2 = ren27 ? out7 : 16'bz;  // Controlled_Buffer controlled_buffer_16
  // Probe on {16{1'b0}}
  // Probe on out3
  SingleReg singlereg_5 (.clk(clk), .WE(WEn3), .Reset(Reset), .RegIn(WriteData), .RegOut(out3));
  // Probe on out7
  SingleReg singlereg_6 (.clk(clk), .WE(WEn7), .Reset(Reset), .RegIn(WriteData), .RegOut(out7));
  and and_1 (WEn0, en0, RegWriteEnable);
  and and_2 (WEn1, en1, RegWriteEnable);
  and and_3 (WEn2, en2, RegWriteEnable);
  and and_4 (WEn3, en3, RegWriteEnable);
  and and_5 (WEn4, en4, RegWriteEnable);
  and and_6 (WEn5, en5, RegWriteEnable);
  and and_7 (WEn6, en6, RegWriteEnable);
  and and_8 (WEn7, en7, RegWriteEnable);
  // Probe on out4
  SingleReg singlereg_7 (.clk(clk), .WE(WEn4), .Reset(Reset), .RegIn(WriteData), .RegOut(out4));

  // Other names for the same wires on the sheet: WriteDat[15:0] = WriteData
endmodule

module SingleAdder (
  input  sub,
  input  A,
  input  B,
  output result,
  output ovf
);

  wire and_1_out, and_2_out, xor_1_out;

  and and_1 (and_1_out, B, A);
  xor xor_1 (xor_1_out, A, B);
  or or_1 (ovf, and_1_out, and_2_out);
  and and_2 (and_2_out, xor_1_out, sub);
  xor xor_2 (result, sub, xor_1_out);
endmodule

module FullAdder (
  input  sub,
  input  [15:0] B,
  input  [15:0] A,
  output ovf,
  output [15:0] result
);

  wire singleadder_1_ovf, singleadder_2_ovf, singleadder_3_ovf, singleadder_4_ovf, singleadder_5_ovf,
       singleadder_6_ovf, singleadder_7_ovf, singleadder_8_ovf, singleadder_9_ovf, singleadder_10_ovf,
       singleadder_11_ovf, singleadder_12_ovf, singleadder_13_ovf, singleadder_14_ovf, singleadder_15_ovf,
       singleadder_16_ovf, xor_1_out, xor_2_out, xor_3_out, xor_4_out, xor_5_out, xor_6_out, xor_7_out,
       xor_8_out, xor_9_out, xor_10_out, xor_11_out, xor_12_out, xor_13_out, xor_14_out, xor_15_out,
       xor_16_out;

  SingleAdder singleadder_1 (.sub(sub), .A(A[0]), .B(xor_1_out), .result(result[0]), .ovf(singleadder_1_ovf));
  xor xor_1 (xor_1_out, B[0], sub);
  SingleAdder singleadder_2 (
    .sub(singleadder_1_ovf), .A(A[1]), .B(xor_2_out), .result(result[1]), .ovf(singleadder_2_ovf));
  SingleAdder singleadder_3 (
    .sub(singleadder_2_ovf), .A(A[2]), .B(xor_3_out), .result(result[2]), .ovf(singleadder_3_ovf));
  xor xor_2 (xor_2_out, B[1], sub);
  xor xor_3 (xor_3_out, B[2], sub);
  SingleAdder singleadder_4 (
    .sub(singleadder_3_ovf), .A(A[3]), .B(xor_4_out), .result(result[3]), .ovf(singleadder_4_ovf));
  SingleAdder singleadder_5 (
    .sub(singleadder_4_ovf), .A(A[4]), .B(xor_5_out), .result(result[4]), .ovf(singleadder_5_ovf));
  xor xor_4 (xor_4_out, B[3], sub);
  SingleAdder singleadder_6 (
    .sub(singleadder_5_ovf), .A(A[5]), .B(xor_6_out), .result(result[5]), .ovf(singleadder_6_ovf));
  xor xor_5 (xor_5_out, B[4], sub);
  xor xor_6 (xor_6_out, B[5], sub);
  SingleAdder singleadder_7 (
    .sub(singleadder_6_ovf), .A(A[6]), .B(xor_7_out), .result(result[6]), .ovf(singleadder_7_ovf));
  SingleAdder singleadder_8 (
    .sub(singleadder_7_ovf), .A(A[7]), .B(xor_8_out), .result(result[7]), .ovf(singleadder_8_ovf));
  xor xor_7 (xor_7_out, B[6], sub);
  xor xor_8 (xor_8_out, B[7], sub);
  SingleAdder singleadder_9 (
    .sub(singleadder_8_ovf), .A(A[8]), .B(xor_9_out), .result(result[8]), .ovf(singleadder_9_ovf));
  SingleAdder singleadder_10 (
    .sub(singleadder_9_ovf), .A(A[9]), .B(xor_10_out), .result(result[9]), .ovf(singleadder_10_ovf));
  xor xor_9 (xor_9_out, B[8], sub);
  xor xor_10 (xor_10_out, B[9], sub);
  SingleAdder singleadder_11 (
    .sub(singleadder_10_ovf), .A(A[10]), .B(xor_11_out), .result(result[10]), .ovf(singleadder_11_ovf));
  xor xor_11 (xor_11_out, B[10], sub);
  SingleAdder singleadder_12 (
    .sub(singleadder_11_ovf), .A(A[11]), .B(xor_12_out), .result(result[11]), .ovf(singleadder_12_ovf));
  xor xor_12 (xor_12_out, B[11], sub);
  SingleAdder singleadder_13 (
    .sub(singleadder_12_ovf), .A(A[12]), .B(xor_13_out), .result(result[12]), .ovf(singleadder_13_ovf));
  xor xor_13 (xor_13_out, B[12], sub);
  SingleAdder singleadder_14 (
    .sub(singleadder_13_ovf), .A(A[13]), .B(xor_14_out), .result(result[13]), .ovf(singleadder_14_ovf));
  xor xor_14 (xor_14_out, B[13], sub);
  SingleAdder singleadder_15 (
    .sub(singleadder_14_ovf), .A(A[14]), .B(xor_15_out), .result(result[14]), .ovf(singleadder_15_ovf));
  xor xor_15 (xor_15_out, B[14], sub);
  SingleAdder singleadder_16 (
    .sub(singleadder_15_ovf), .A(A[15]), .B(xor_16_out), .result(result[15]), .ovf(singleadder_16_ovf));
  xor xor_16 (xor_16_out, B[15], sub);
  xor xor_17 (ovf, singleadder_16_ovf, singleadder_15_ovf);

  // Other names for the same wires on the sheet: s0 = result[0]; s1 = result[1]; s2 = result[2]; s3 = result[3];
  //   s4 = result[4]; s5 = result[5]; s6 = result[6]; s7 = result[7]; s8 = result[8]; s9 = result[9];
  //   s10 = result[10]; s11 = result[11]; s12 = result[12]; s13 = result[13]; s14 = result[14]; s15 = result[15]
endmodule

module RS1 (
  input  [15:0] data_in,
  output [15:0] data_out
);


  assign data_out = {1'b0, data_in[15:1]};
endmodule

module RS2 (
  input  [15:0] data_in,
  output [15:0] data_out
);


  assign data_out = {2'b00, data_in[15:2]};
endmodule

module RS4 (
  input  [15:0] data_in,
  output [15:0] data_out
);


  assign data_out = {4'b0000, data_in[15:4]};
endmodule

module RS (
  input  [15:0] in_1,
  input  [2:0] in_2,
  output [15:0] out_3
);

  wire [15:0] one_out, three_in, three_out, two_in, two_out;

  RS1 rs1_1 (.data_in(in_1), .data_out(one_out));
  Multiplexer #(.width(16), .enable("false")) multiplexer_1 (.in0(in_1), .in1(one_out), .out(two_in), .sel(in_2[0]));
  Multiplexer #(.width(16), .enable("false")) multiplexer_2 (
    .in0(two_in), .in1(two_out), .out(three_in), .sel(in_2[1]));
  RS2 rs2_1 (.data_in(two_in), .data_out(two_out));
  Multiplexer #(.width(16), .enable("false")) multiplexer_3 (
    .in0(three_in), .in1(three_out), .out(out_3), .sel(in_2[2]));
  RS4 rs4_1 (.data_in(three_in), .data_out(three_out));

  // Other names for the same wires on the sheet: one_in[15:0] = in_1
endmodule

module LS1 (
  input  [15:0] data_in,
  output [15:0] data_out
);


  assign data_out = {data_in[14:0], 1'b0};
endmodule

module LS2 (
  input  [15:0] data_in,
  output [15:0] data_out
);


  assign data_out = {data_in[13:0], 2'b00};
endmodule

module LS4 (
  input  [15:0] data_in,
  output [15:0] data_out
);


  assign data_out = {data_in[11:0], 4'b0000};
endmodule

module LS (
  input  [15:0] in_1,
  input  [2:0] in_2,
  output [15:0] out_3
);

  wire [15:0] one_out, three_in, three_out, two_in, two_out;

  Multiplexer #(.width(16), .enable("false")) multiplexer_1 (.in0(in_1), .in1(one_out), .out(two_in), .sel(in_2[0]));
  Multiplexer #(.width(16), .enable("false")) multiplexer_2 (
    .in0(two_in), .in1(two_out), .out(three_in), .sel(in_2[1]));
  LS1 ls1_1 (.data_in(in_1), .data_out(one_out));
  Multiplexer #(.width(16), .enable("false")) multiplexer_3 (
    .in0(three_in), .in1(three_out), .out(out_3), .sel(in_2[2]));
  LS2 ls2_1 (.data_in(two_in), .data_out(two_out));
  LS4 ls4_1 (.data_in(three_in), .data_out(three_out));

  // Other names for the same wires on the sheet: one_in[15:0] = in_1
endmodule

module EqualCheck (
  input  [15:0] r1,
  input  [15:0] r2,
  output result
);

  wire fulladder_1_ovf, nor_1_out, not_1_out, not_2_out, not_3_out, not_4_out, not_5_out, not_6_out,
       not_7_out, not_8_out, not_9_out, not_10_out, not_11_out, not_12_out, not_13_out, not_14_out,
       not_15_out;
  wire [15:0] fulladder_1_result;

  FullAdder fulladder_1 (.sub(1'b1), .B(r1), .A(r2), .ovf(fulladder_1_ovf), .result(fulladder_1_result));
  not not_1 (not_1_out, fulladder_1_result[0]);
  not not_2 (not_2_out, fulladder_1_result[1]);
  not not_3 (not_3_out, fulladder_1_result[2]);
  not not_4 (not_4_out, fulladder_1_result[3]);
  not not_5 (not_5_out, fulladder_1_result[4]);
  not not_6 (not_6_out, fulladder_1_result[5]);
  not not_7 (not_7_out, fulladder_1_result[12]);
  not not_8 (not_8_out, fulladder_1_result[13]);
  not not_9 (not_9_out, fulladder_1_result[14]);
  nor nor_1 (nor_1_out, fulladder_1_result[15], fulladder_1_ovf);
  not not_10 (not_10_out, fulladder_1_result[6]);
  not not_11 (not_11_out, fulladder_1_result[7]);
  not not_12 (not_12_out, fulladder_1_result[8]);
  not not_13 (not_13_out, fulladder_1_result[9]);
  not not_14 (not_14_out, fulladder_1_result[10]);
  not not_15 (not_15_out, fulladder_1_result[11]);
  and and_1 (result, not_1_out, not_2_out, not_3_out, not_4_out, not_5_out, not_6_out, not_10_out, not_11_out, not_12_out, not_13_out, not_14_out, not_15_out, not_7_out, not_8_out, not_9_out, nor_1_out);
endmodule

module LessThanCheck (
  input  [15:0] r1,
  input  [15:0] r2,
  output result
);

  wire [14:0] fulladder_1_result;

  FullAdder fulladder_1 (.sub(1'b1), .B(r2), .A(r1), .result({result, fulladder_1_result}));  // open: ovf
endmodule

module ALU_circ (
  input  [15:0] A,
  input  [15:0] B,
  input  [2:0] shamt,
  input  [2:0] optype,
  output [15:0] out_put
);

  wire o, o_21d941f3;
  wire [15:0] and_1_out, ls_1_out_3, not_1_out, or_1_out, r, r_457bd0b6, rs_1_out_3;

  assign not_1_out = ~A;  // NOT_Gate not_1, 16 bits wide
  FullAdder fulladder_1 (.sub(1'b1), .B(B), .A(A), .ovf(o), .result(r));
  assign or_1_out = A | B;  // OR_Gate or_1, 16 bits wide
  assign and_1_out = A & B;  // AND_Gate and_1, 16 bits wide
  LS ls_1 (.in_1(A), .in_2(shamt), .out_3(ls_1_out_3));
  RS rs_1 (.in_1(A), .in_2(shamt), .out_3(rs_1_out_3));
  Multiplexer #(.select(3), .width(16), .enable("false")) multiplexer_1 (
    .in0(or_1_out), .in1(and_1_out), .in2(r_457bd0b6), .in3(r), .in4(ls_1_out_3), .in5(rs_1_out_3),
    .in6(not_1_out), .out(out_put), .sel(optype));  // open: in7
  FullAdder fulladder_2 (.sub(1'b0), .B(B), .A(A), .ovf(o_21d941f3), .result(r_457bd0b6));

  // Other names for the same wires on the sheet: a_f858d4a7[15:0] = A; b_6bd245bf[15:0] = B
endmodule

module memory_latch (
  input  [15:0] address,
  input  WE,
  input  clk,
  input  [15:0] data_in,
  output [15:0] address_latched,
  output WE_latched,
  output OE_latched,
  output [15:0] data_in_latched
);

  wire DMwe_latch_q;
  wire [15:0] addr_latch_q;

  Register #(.width(16), .trigger("falling")) addr_latch (
    .D(address), .en(WE), .clk(clk), .Q(addr_latch_q));  // open: clr
  D_Flip_Flop #(.trigger("falling")) DMwe_latch (.D(WE), .clk(clk), .Q(DMwe_latch_q));  // open: Qn, preset, reset
  Register #(.width(16), .trigger("falling")) data_to_be_written (
    .D(data_in), .en(WE), .clk(clk), .Q(data_in_latched));  // open: clr
  Multiplexer #(.width(16), .enable("false")) multiplexer_1 (
    .in0(address), .in1(addr_latch_q), .out(address_latched), .sel(DMwe_latch_q));
  and and_1 (WE_latched, clk, DMwe_latch_q);
  not not_1 (OE_latched, WE_latched);
endmodule

module main (
  input  in_1
);

  wire Falling, Rising;
  wire [3:0] rom_1_data;
  wire [11:0] Address;
  wire [15:0] Next_PC, PC;

  Clock clock_1 (.out(Rising));
  not not_1 (Falling, Rising);
  ROM #(.addrWidth(16), .dataWidth(16)) rom_1 (.addr(PC), .data({rom_1_data, Address}));
  SingleReg singlereg_1 (.clk(Rising), .WE(1'b1), .Reset(in_1), .RegOut(PC));  // open: RegIn
  FullAdder fulladder_1 (.B(16'h1), .A(PC), .result(Next_PC));  // open: sub, ovf

  // Other names for the same wires on the sheet: Rd[2:0] = Address[5:3]; Reset = in_1; Rs[2:0] = Address[11:9];
  //   Rt[2:0] = Address[8:6]; Shamt[2:0] = Address[2:0]

  // Notes on the sheet:
  //   contents of rom_1 (hex, n*v repeats v):
  //   7000 6083 60c4 6100 b825 6900 b825 6900 b821 6900 1880 18c1 6080 60c0 880 8c1 203f
endmodule

module main2 (
  input  in_1
);

  wire Falling, memory_latch_1_we_latched, Rising;
  wire [11:0] Address;
  wire [15:0] in_PC, NextPC, PC;
  wire [15:12] Instruction_Memory_data;

  Clock clock_1 (.out(Rising));
  not not_1 (Falling, Rising);
  ROM #(.addrWidth(16), .dataWidth(16)) Instruction_Memory (.addr(PC), .data({Instruction_Memory_data, Address}));
  SingleReg singlereg_1 (.clk(Rising), .WE(1'b1), .Reset(in_1), .RegIn(in_PC), .RegOut(PC));
  FullAdder fulladder_1 (.sub(1'b0), .B(16'h1), .A(PC), .result(NextPC));  // open: ovf
  RegisterFile registerfile_1 ();  // open: clk, Reset, WriteData, WriteReg, ReadReg1, ReadReg2, RegWriteEnable, ReadData1, ReadData2
  memory_latch memory_latch_1 (.WE_latched(memory_latch_1_we_latched));  // open: address, WE, clk, data_in, address_latched, OE_latched, data_in_latched
  RAM #(.addrWidth(16), .dataWidth(16)) Data_Memory (.ld(memory_latch_1_we_latched));  // open: addr, data, sel, clk, clr

  // Other names for the same wires on the sheet: Immediate[5:0] = Address[5:0]; Shamt[2:0] = Address[2:0];
  //   Rd[2:0] = Address[5:3]; Rt[2:0] = Address[8:6]; Rs[2:0] = Address[11:9]; Reset = in_1

  // Notes on the sheet:
  //   contents of Instruction_Memory (hex, n*v repeats v):
  //   7000 6083 60c4 6100 b825 6900 b825 6900 b821 6900 1880 18c1 6080 60c0 880 8c1 203f
endmodule

module main3 (
  input  in_1
);

  wire ALUinB, and_1_out, and_2_out, ble, bne, DMwe, eqcheck, Falling, in_put, j, jal, jr, keyboard_1_avail,
       Leq, LessCheck, memory_latch_1_oe_latched, memory_latch_1_we_latched, neqcheck, or_2_out, or_3_out,
       out_put, Rdst, Rising, Rwd, Rwe;
  wire [2:0] ALUop, multiplexer_2_out, multiplexer_5_out;
  wire [3:0] opcode;
  wire [6:0] keyboard_1_data;
  wire [11:0] address;
  wire [15:0] Adder__result, ALU_out, bit_extender_1_out, memory_latch_1_address_latched,
       memory_latch_1_data_in_latched, multiplexer_1_out, multiplexer_3_out, multiplexer_4_out,
       multiplexer_7_out, multiplexer_8_out, multiplexer_9_out, multiplexer_10_out, my_input, NextPC,
       PC_regout, R1, R2, ram_1_dout;

  Multiplexer #(.width(16), .enable("false")) multiplexer_1 (
    .in0(multiplexer_9_out), .in1(R1), .out(multiplexer_1_out), .sel(jr));
  Clock clock_1 (.out(Rising));
  not not_1 (Falling, Rising);
  SingleReg PC (.clk(Falling), .WE(1'b1), .Reset(in_1), .RegIn(multiplexer_1_out), .RegOut(PC_regout));
  ROM #(.addrWidth(16), .dataWidth(16)) Instr_Mem (.addr(PC_regout), .data({opcode, address}));
  FullAdder Adder (.B(16'h1), .A(PC_regout), .result(NextPC));  // open: sub, ovf
  Multiplexer #(.width(3), .enable("false")) multiplexer_2 (
    .in0(address[8:6]), .in1(address[5:3]), .out(multiplexer_2_out), .sel(Rdst));
  Keyboard keyboard_1 (.clk(Falling), .re(in_put), .clr(in_1), .avail(keyboard_1_avail), .data(keyboard_1_data));
  Multiplexer #(.width(16), .enable("false")) multiplexer_3 (
    .in0(multiplexer_10_out), .in1(my_input), .out(multiplexer_3_out), .sel(in_put));
  Multiplexer #(.width(16), .enable("false")) multiplexer_4 (
    .in0(multiplexer_3_out), .in1(NextPC), .out(multiplexer_4_out), .sel(jal));
  Multiplexer #(.width(3), .enable("false")) multiplexer_5 (
    .in0(multiplexer_2_out), .in1(3'b111), .out(multiplexer_5_out), .sel(jal));
  or or_1 (Leq, LessCheck, eqcheck);
  my_control Control (
    .in_1(opcode), .ble(ble), .bne(bne), .Rwd(Rwd), .Rdst(Rdst), .j(j), .DMwe(DMwe), .Rwe(Rwe),
    .out_put(out_put), .jal(jal), .jr(jr), .ALUinB(ALUinB), .in_put(in_put), .ALUop(ALUop));
  EqualCheck equalcheck_1 (.r1(R1), .r2(R2), .result(eqcheck));
  LessThanCheck lessthancheck_1 (.r1(R1), .r2(R2), .result(LessCheck));
  Multiplexer #(.width(16), .enable("false")) multiplexer_6 (
    .in0(16'h40), .in1({{9{1'b0}}, keyboard_1_data}), .out(my_input), .sel(keyboard_1_avail));
  not not_2 (neqcheck, eqcheck);
  RegisterFile Register_File (
    .clk(Rising), .Reset(in_1), .WriteData(multiplexer_4_out), .WriteReg(multiplexer_5_out),
    .ReadReg1(address[11:9]), .ReadReg2(address[8:6]), .RegWriteEnable(Rwe), .ReadData1(R1), .ReadData2(R2));
  assign bit_extender_1_out = {{10{address[5]}}, address[5:0]};  // Bit_Extender bit_extender_1
  Multiplexer #(.width(16), .enable("false")) multiplexer_7 (
    .in0(R2), .in1(bit_extender_1_out), .out(multiplexer_7_out), .sel(ALUinB));
  FullAdder Adder_ (.B(NextPC), .A(bit_extender_1_out), .result(Adder__result));  // open: sub, ovf
  and and_1 (and_1_out, ble, Leq);
  Multiplexer #(.width(16), .enable("false")) multiplexer_8 (
    .in0(NextPC), .in1(Adder__result), .out(multiplexer_8_out), .sel(or_2_out));
  or or_2 (or_2_out, and_1_out, and_2_out);
  and and_2 (and_2_out, bne, neqcheck);
  memory_latch memory_latch_1 (
    .address(ALU_out), .WE(DMwe), .clk(Falling), .data_in(R2),
    .address_latched(memory_latch_1_address_latched), .WE_latched(memory_latch_1_we_latched),
    .OE_latched(memory_latch_1_oe_latched), .data_in_latched(memory_latch_1_data_in_latched));
  Multiplexer #(.width(16), .enable("false")) multiplexer_9 (
    .in0(multiplexer_8_out), .in1({NextPC[15:12], address}), .out(multiplexer_9_out), .sel(or_3_out));
  RAM #(.addrWidth(16), .dataWidth(16), .trigger("high"), .databus("bibus")) ram_1 (
    .addr(memory_latch_1_address_latched), .we(memory_latch_1_we_latched), .oe(memory_latch_1_oe_latched),
    .din(memory_latch_1_data_in_latched), .dout(ram_1_dout));
  ALU_circ ALU (.A(R1), .B(multiplexer_7_out), .shamt(address[2:0]), .optype(ALUop), .out_put(ALU_out));
  or or_3 (or_3_out, j, jr, jal);
  Multiplexer #(.width(16), .enable("false")) multiplexer_10 (
    .in0(ALU_out), .in1(ram_1_dout), .out(multiplexer_10_out), .sel(Rwd));
  TTY #(.rows(13), .cols(80)) tty_1 (.data(R1[6:0]), .clk(Rising), .we(out_put), .clr(in_1));

  // Other names for the same wires on the sheet: immediate[5:0] = address[5:0]; Shamt[2:0] = address[2:0];
  //   Rd[2:0] = address[5:3]; Rt[2:0] = address[8:6]; Rs[2:0] = address[11:9]; Reset = in_1
endmodule

module my_control (
  input  [3:0] in_1,
  output ble,
  output bne,
  output Rwd,
  output Rdst,
  output j,
  output DMwe,
  output Rwe,
  output out_put,
  output jal,
  output jr,
  output ALUinB,
  output in_put,
  output [2:0] ALUop
);

  wire decoder_1_out0, decoder_1_out1, decoder_1_out2, decoder_1_out3, decoder_1_out4, decoder_1_out5,
       decoder_1_out6, decoder_1_out11, decoder_1_out14;

  Decoder #(.select(4)) decoder_1 (
    .out0(decoder_1_out0), .out1(decoder_1_out1), .out2(decoder_1_out2), .out3(decoder_1_out3),
    .out4(decoder_1_out4), .out5(decoder_1_out5), .out6(decoder_1_out6), .out7(Rwd), .out8(DMwe), .out9(bne),
    .out10(ble), .out11(decoder_1_out11), .out12(jr), .out13(jal), .out14(decoder_1_out14), .out15(out_put),
    .sel(in_1));  // open: en
  or or_1 (j, jal, jr, decoder_1_out11);
  or or_2 (ALUinB, decoder_1_out1, Rwd, DMwe);
  or or_3 (Rwe, decoder_1_out0, decoder_1_out1, decoder_1_out2, decoder_1_out3, decoder_1_out4, decoder_1_out5, decoder_1_out6, Rwd, decoder_1_out14, jal);
  or or_4 (Rdst, decoder_1_out0, decoder_1_out2, decoder_1_out3, decoder_1_out4, decoder_1_out5, decoder_1_out6);
  or or_5 (ALUop[2], decoder_1_out3, decoder_1_out4, decoder_1_out6, ble);
  or or_6 (ALUop[1], decoder_1_out0, decoder_1_out1, decoder_1_out2, decoder_1_out6, Rwd, DMwe, bne);
  or or_7 (ALUop[0], decoder_1_out2, decoder_1_out4, decoder_1_out5, bne);
  buf or_8 (in_put, decoder_1_out14);  // OR_Gate

  // Notes on the sheet:
  //   add
  //   addi
  //   sub
  //   sll
  //   srl
  //   and
  //   not
  //   lw
  //   sw
  //   bne
  //   ble
  //   j
  //   jr
  //   jal
  //   input
  //   output
endmodule
