// Logisim project my_adder.circ as structural Verilog: 2 circuits, main circuit main
module full_adder (
  input  sub,
  input  A,
  input  B,
  output result,
  output ovf
);

  wire and_1_out, and_2_out, xor_1_out;

  and and_1 (and_1_out, B, A);
  xor xor_1 (xor_1_out, A, B);
  or or_1 (ovf, and_1_out, and_2_out);
  and and_2 (and_2_out, xor_1_out, sub);
  xor xor_2 (result, sub, xor_1_out);
endmodule

module main (
  input  sub,
  input  [15:0] B,
  input  [15:0] A,
  output ovf,
  output [15:0] result
);

  wire full_adder_1_ovf, full_adder_2_ovf, full_adder_3_ovf, full_adder_4_ovf, full_adder_5_ovf,
       full_adder_6_ovf, full_adder_7_ovf, full_adder_8_ovf, full_adder_9_ovf, full_adder_10_ovf,
       full_adder_11_ovf, full_adder_12_ovf, full_adder_13_ovf, full_adder_14_ovf, full_adder_15_ovf,
       full_adder_16_ovf, xor_1_out, xor_2_out, xor_3_out, xor_4_out, xor_5_out, xor_6_out, xor_7_out,
       xor_8_out, xor_9_out, xor_10_out, xor_11_out, xor_12_out, xor_13_out, xor_14_out, xor_15_out,
       xor_16_out;

  full_adder full_adder_1 (.sub(sub), .A(A[0]), .B(xor_1_out), .result(result[0]), .ovf(full_adder_1_ovf));
  xor xor_1 (xor_1_out, B[0], sub);
  full_adder full_adder_2 (.sub(full_adder_1_ovf), .A(A[1]), .B(xor_2_out), .result(result[1]), .ovf(full_adder_2_ovf));
  full_adder full_adder_3 (.sub(full_adder_2_ovf), .A(A[2]), .B(xor_3_out), .result(result[2]), .ovf(full_adder_3_ovf));
  xor xor_2 (xor_2_out, B[1], sub);
  xor xor_3 (xor_3_out, B[2], sub);
  full_adder full_adder_4 (.sub(full_adder_3_ovf), .A(A[3]), .B(xor_4_out), .result(result[3]), .ovf(full_adder_4_ovf));
  full_adder full_adder_5 (.sub(full_adder_4_ovf), .A(A[4]), .B(xor_5_out), .result(result[4]), .ovf(full_adder_5_ovf));
  xor xor_4 (xor_4_out, B[3], sub);
  full_adder full_adder_6 (.sub(full_adder_5_ovf), .A(A[5]), .B(xor_6_out), .result(result[5]), .ovf(full_adder_6_ovf));
  xor xor_5 (xor_5_out, B[4], sub);
  xor xor_6 (xor_6_out, B[5], sub);
  full_adder full_adder_7 (.sub(full_adder_6_ovf), .A(A[6]), .B(xor_7_out), .result(result[6]), .ovf(full_adder_7_ovf));
  full_adder full_adder_8 (.sub(full_adder_7_ovf), .A(A[7]), .B(xor_8_out), .result(result[7]), .ovf(full_adder_8_ovf));
  xor xor_7 (xor_7_out, B[6], sub);
  xor xor_8 (xor_8_out, B[7], sub);
  full_adder full_adder_9 (.sub(full_adder_8_ovf), .A(A[8]), .B(xor_9_out), .result(result[8]), .ovf(full_adder_9_ovf));
  full_adder full_adder_10 (
    .sub(full_adder_9_ovf), .A(A[9]), .B(xor_10_out), .result(result[9]), .ovf(full_adder_10_ovf));
  xor xor_9 (xor_9_out, B[8], sub);
  xor xor_10 (xor_10_out, B[9], sub);
  full_adder full_adder_11 (
    .sub(full_adder_10_ovf), .A(A[10]), .B(xor_11_out), .result(result[10]), .ovf(full_adder_11_ovf));
  xor xor_11 (xor_11_out, B[10], sub);
  full_adder full_adder_12 (
    .sub(full_adder_11_ovf), .A(A[11]), .B(xor_12_out), .result(result[11]), .ovf(full_adder_12_ovf));
  xor xor_12 (xor_12_out, B[11], sub);
  full_adder full_adder_13 (
    .sub(full_adder_12_ovf), .A(A[12]), .B(xor_13_out), .result(result[12]), .ovf(full_adder_13_ovf));
  xor xor_13 (xor_13_out, B[12], sub);
  full_adder full_adder_14 (
    .sub(full_adder_13_ovf), .A(A[13]), .B(xor_14_out), .result(result[13]), .ovf(full_adder_14_ovf));
  xor xor_14 (xor_14_out, B[13], sub);
  full_adder full_adder_15 (
    .sub(full_adder_14_ovf), .A(A[14]), .B(xor_15_out), .result(result[14]), .ovf(full_adder_15_ovf));
  xor xor_15 (xor_15_out, B[14], sub);
  full_adder full_adder_16 (
    .sub(full_adder_15_ovf), .A(A[15]), .B(xor_16_out), .result(result[15]), .ovf(full_adder_16_ovf));
  xor xor_16 (xor_16_out, B[15], sub);
  xor xor_17 (ovf, full_adder_16_ovf, full_adder_15_ovf);

  // Other names for the same wires on the sheet: s0 = result[0]; s1 = result[1]; s2 = result[2]; s3 = result[3];
  //   s4 = result[4]; s5 = result[5]; s6 = result[6]; s7 = result[7]; s8 = result[8]; s9 = result[9];
  //   s10 = result[10]; s11 = result[11]; s12 = result[12]; s13 = result[13]; s14 = result[14]; s15 = result[15]
endmodule
